# Fritzing sketch Spotwelder (saved by Fritzing 0.9.10b)
circuit board: 8.46667cm x 5.64444cm
breadboards: 1

parts:
  Part1 = Arduino Nano (Rev3.0)
  Q1 = PNP-Transistor [package="TO92 [THT]"]
  R1 = Resistor [tolerance=±5% power=0.25 resistance=10k package=THT]
  R2 = Resistor [tolerance=±5% resistance=1k package="0402 [SMD]"]
  S1 = Pushbutton [package="[THT]"]
  L1 = Solenoid

nets:
  N1: Part1.GND, Q1.C, R1.Pin_1
  N2: Part1.D2, S1.Pin_3, S1.Pin_4
  N3: Part1.5V, S1.Pin_1, S1.Pin_2
  N4: Part1.D13/SCK, R2.Pin_0
  N5: Q1.E, R1.Pin_0, R2.Pin_1
  N6: Q1.B, L1.pin1
